# Fritzing sketch sonic_volume (saved by Fritzing 0.9.3b)
breadboards: 1

parts:
  T-Cobbler1 = T-Cobbler
  module1 = Dule-Color LED
  元件2 = SRF05 Ultrasonic Rangefinder
  Raspberry_Pi_1 = Raspberry Pi 3 [part_number=RPI-3-V1.2]  # not connected
  SPKR1 = Loudspeaker  # not connected

nets:
  N1: T-Cobbler1.GPIO17, 元件2.Trig
  N2: T-Cobbler1.GPIO13, module1.G
  N3: T-Cobbler1.5V0#20, 元件2.VCC
  GND: T-Cobbler1.GND#22, module1.GND, 元件2.GND
  N4: T-Cobbler1.GPIO18, module1.R
  N5: T-Cobbler1.GPIO24, 元件2.Echo

notes:
  Dual-Color LED
  Ultrasonic Ranging

custom parts:
  T-Cobbler: T-Cobbler for RPi B+ and Rpi2 from SunFounder
  Dule-Color LED: DuleColor LED module of SunFounder Sensor Kit
